// Logisim project third.circ as structural Verilog: 11 circuits, main circuit main
module main (
  input  [31:0] a,
  input  [31:0] b,
  input  [3:0] aluop,
  input  output_inverted,
  input  output_inc,
  input  clk,
  input  rst,
  output [31:0] res_low,
  output done,
  output [31:0] res_high
);

  wire adder_2_cout, comparator_1_eq, comparator_2_eq, comparator_3_eq, comparator_4_eq, comparator_5_eq,
       done_DIV, done_MULT, not_2_out, not_3_out, not_4_out, or_1_out, or_2_out, start, SUB_cout;
  wire [0:0] ADD_HIGH;
  wire [3:0] aluop_Reg_q;
  wire [31:0] a_Reg_q, ADD_LOW, adder_1_out, adder_2_out, AND_LOW, ASR_HIGH, ASR_LOW, b_Reg_q, DIV_HIGH,
       DIV_LOW, LSL_HIGH, LSL_LOW, LSR_HIGH, LSR_LOW, MUL_HIGH, MUL_LOW, multiplexer_2_out,
       multiplexer_3_out, multiplexer_4_out, multiplexer_5_out, not_1_out, not_5_out, not_6_out, OR_LOW,
       ROTR_HIGH, ROTR_LOW, SUB_HIGH, SUB_LOW, undriven, undriven_2, undriven_3, undriven_4, undriven_5,
       undriven_6, undriven_7, undriven_8, undriven_9, undriven_10, XOR_LOW;

  assign not_1_out = ~b;  // NOT_Gate not_1, 32 bits wide
  Register #(.width(32)) a_Reg (.D(a), .clk(clk), .Q(a_Reg_q));  // open: en, clr
  Register #(.width(32)) b_Reg (.D(b), .clk(clk), .Q(b_Reg_q));  // open: en, clr
  Register #(.width(4)) aluop_Reg (.D(aluop), .clk(clk), .Q(aluop_Reg_q));  // open: en, clr
  CSA Sum (.a(a), .b(b), .s(ADD_LOW), .cout(ADD_HIGH[0]));  // open: cin
  CSA SUB (.cin(1'b1), .a(a), .b(not_1_out), .s(SUB_LOW), .cout(SUB_cout));
  not not_2 (not_2_out, comparator_1_eq);
  Comparator #(.width(32)) comparator_1 (.a(a_Reg_q), .b(a), .eq(comparator_1_eq));  // open: gt, lt
  not not_3 (not_3_out, comparator_2_eq);
  Comparator #(.width(32)) comparator_2 (.a(b_Reg_q), .b(b), .eq(comparator_2_eq));  // open: gt, lt
  not not_4 (not_4_out, comparator_3_eq);
  Comparator #(.width(4)) comparator_3 (.a(aluop_Reg_q), .b(aluop), .eq(comparator_3_eq));  // open: gt, lt
  Multiplexer #(.width(32)) multiplexer_1 (.in0({32{1'b1}}), .in1({32{1'b0}}), .out(SUB_HIGH), .sel(SUB_cout));
  LSR Logical_Shift_Right (.a(a), .b(b), .shifted({LSR_HIGH, LSR_LOW}));
  LSL Logical_Shift_Left (.a(a), .b(b), .shifted({LSL_HIGH, LSL_LOW}));
  or or_1 (or_1_out, not_2_out, not_4_out, not_3_out);
  Comparator #(.width(4)) comparator_4 (.a(aluop), .b(4'b0010), .eq(comparator_4_eq));  // open: gt, lt
  Comparator #(.width(4)) comparator_5 (.a(aluop), .b(4'b0011), .eq(comparator_5_eq));  // open: gt, lt
  or or_2 (or_2_out, comparator_4_eq, comparator_5_eq);
  Multiplexer #(.select(4), .width(32)) multiplexer_2 (
    .in0(ADD_LOW), .in1(SUB_LOW), .in2(MUL_LOW), .in3(DIV_LOW), .in4(AND_LOW), .in5(OR_LOW), .in6(XOR_LOW),
    .in7(undriven_6), .in8(undriven_7), .in9(LSL_LOW), .in10(LSR_LOW), .in11(ASR_LOW), .in12(ROTR_LOW),
    .in13(undriven_8), .in14(undriven_9), .in15(undriven_10), .out(multiplexer_2_out), .sel(aluop));
  Multiplexer #(.select(4), .width(32)) multiplexer_3 (
    .in0({{31{1'b0}}, ADD_HIGH[0]}), .in1(SUB_HIGH), .in2(MUL_HIGH), .in3(DIV_HIGH), .in4({32{1'b0}}),
    .in5({32{1'b0}}), .in6({32{1'b0}}), .in7(undriven), .in8(undriven_2), .in9(LSL_HIGH), .in10(LSR_HIGH),
    .in11(ASR_HIGH), .in12(ROTR_HIGH), .in13(undriven_3), .in14(undriven_4), .in15(undriven_5),
    .out(multiplexer_3_out), .sel(aluop));
  and and_1 (start, or_1_out, or_2_out);
  assign not_5_out = ~multiplexer_2_out;  // NOT_Gate not_5, 32 bits wide
  Multiplexer #(.width(32)) multiplexer_4 (
    .in0(multiplexer_3_out), .in1(not_6_out), .out(multiplexer_4_out), .sel(output_inverted));
  assign not_6_out = ~multiplexer_3_out;  // NOT_Gate not_6, 32 bits wide
  Multiplexer #(.width(32)) multiplexer_5 (
    .in0(multiplexer_2_out), .in1(not_5_out), .out(multiplexer_5_out), .sel(output_inverted));
  Adder #(.width(32)) adder_1 (
    .a(multiplexer_4_out), .b({32{1'b0}}), .out(adder_1_out), .cin(adder_2_cout));  // open: cout
  mul Multiplier (.clk(clk), .start(start), .a(a), .b(b), .done(done_MULT), .Result({MUL_HIGH, MUL_LOW}));
  Div Divider (
    .start(start), .clk(clk), .dividend(a), .divisor(b), .done(done_DIV), .remainder(DIV_HIGH),
    .quotient(DIV_LOW));
  ASR Arithmetic_Shift_Right (.a(a), .b(b), .shifted({ASR_HIGH, ASR_LOW}));
  ROT_R Rotate_Right (.a(a), .b(b), .rotated({ROTR_HIGH, ROTR_LOW}));
  Adder #(.width(32)) adder_2 (.a(multiplexer_5_out), .b(32'h1), .out(adder_2_out), .cout(adder_2_cout));  // open: cin
  Multiplexer #(.width(32)) multiplexer_6 (
    .in0(multiplexer_4_out), .in1(adder_1_out), .out(res_high), .sel(output_inc));
  Multiplexer #(.width(32)) multiplexer_7 (.in0(multiplexer_5_out), .in1(adder_2_out), .out(res_low), .sel(output_inc));
  assign AND_LOW = a & b;  // AND_Gate and_2, 32 bits wide
  assign OR_LOW = a | b;  // OR_Gate or_3, 32 bits wide
  assign XOR_LOW = a ^ b;  // XOR_Gate xor_1, 32 bits wide

  assign done = 1'b1;

  // Other names for the same wires on the sheet: inc = output_inc; invert = output_inverted
endmodule

module counter2 (
  input  clk,
  input  reset,
  output num
);

  wire adder_1_out;

  Adder #(.width(1)) adder_1 (.a(num), .b(1'b1), .out(adder_1_out));  // open: cin, cout
  Register #(.width(1)) register_1 (.D(adder_1_out), .clk(clk), .Q(num), .clr(reset));  // open: en
endmodule

module Div (
  input  start,
  input  clk,
  input  [31:0] dividend,
  input  [31:0] divisor,
  output done,
  output [31:0] remainder,
  output [31:0] quotient
);

  wire comparator_1_gt, comparator_2_lt, counter_div_num, not_1_out, not_3_out, undriven;
  wire [7:0] adder_1_out, counter_q;
  wire [31:0] adder_2_out, multiplexer_1_out, multiplexer_2_out, multiplexer_3_out, multiplexer_4_out,
       multiplexer_5_out, shifter_1_out, shifter_1_out_2, subtractor_1_out;
  wire [63:0] q_q;

  not not_1 (not_1_out, counter_div_num);
  Multiplexer #(.width(32)) multiplexer_1 (
    .in0(q_q[31:0]), .in1(adder_2_out), .out(multiplexer_1_out), .sel(not_3_out));
  Adder adder_1 (.a(counter_q), .b(8'h1), .out(adder_1_out));  // open: cin, cout
  Register counter (.D(adder_1_out), .en(not_1_out), .clk(clk), .Q(counter_q), .clr(start));
  Multiplexer #(.width(32)) multiplexer_2 (
    .in0(shifter_1_out_2), .in1(multiplexer_3_out), .out(multiplexer_2_out), .sel(counter_div_num));
  Multiplexer #(.width(32)) multiplexer_3 (
    .in0(q_q[63:32]), .in1(subtractor_1_out), .out(multiplexer_3_out), .sel(not_3_out));
  Multiplexer #(.width(32)) multiplexer_4 (
    .in0(shifter_1_out), .in1(multiplexer_1_out), .out(multiplexer_4_out), .sel(counter_div_num));
  Multiplexer #(.width(32)) multiplexer_5 (
    .in0(multiplexer_4_out), .in1(dividend), .out(multiplexer_5_out), .sel(start));
  Register #(.width(32)) a (.D(multiplexer_2_out), .en(done), .clk(clk), .Q(q_q[63:32]), .clr(start));
  Register #(.width(32)) q (.D(multiplexer_5_out), .en(done), .clk(clk), .Q(q_q[31:0]), .clr(undriven));
  counter2 counter_div (.clk(clk), .reset(start), .num(counter_div_num));
  Comparator comparator_1 (.a(counter_q), .b(8'h20), .gt(comparator_1_gt));  // open: eq, lt
  Comparator #(.mode("unsigned"), .width(32)) comparator_2 (
    .a(q_q[63:32]), .b(divisor), .lt(comparator_2_lt));  // open: gt, eq
  not not_2 (done, comparator_1_gt);
  Shifter #(.width(64)) shifter_1 (.in(q_q), .\dist (6'b000001), .out({shifter_1_out_2, shifter_1_out}));
  not not_3 (not_3_out, comparator_2_lt);
  Register #(.width(32)) register_1 (.D(q_q[63:32]), .en(done), .clk(clk), .Q(remainder));  // open: clr
  Subtractor #(.width(32)) subtractor_1 (.a(q_q[63:32]), .b(divisor), .out(subtractor_1_out));  // open: bin, bout
  Adder #(.width(32)) adder_2 (.a(q_q[31:0]), .b(32'h1), .out(adder_2_out));  // open: cin, cout
  Register #(.width(32)) register_2 (.D(q_q[31:0]), .en(done), .clk(clk), .Q(quotient));  // open: clr
endmodule

module CSA (
  input  cin,
  input  [31:0] a,
  input  [31:0] b,
  output [31:0] s,
  output cout
);

  wire adder_1_cout, adder_2_cout, adder_3_cout, adder_4_cout, adder_5_cout, adder_6_cout, adder_7_cout,
       multiplexer_2_out, multiplexer_3_out;
  wire [7:0] adder_2_out, adder_3_out, adder_4_out, adder_5_out, adder_6_out, adder_7_out;

  Adder adder_1 (.a(a[7:0]), .b(b[7:0]), .out(s[7:0]), .cin(cin), .cout(adder_1_cout));
  Adder adder_2 (.a(a[15:8]), .b(b[15:8]), .out(adder_2_out), .cout(adder_2_cout));  // open: cin
  Adder adder_3 (.a(a[15:8]), .b(b[15:8]), .out(adder_3_out), .cin(1'b1), .cout(adder_3_cout));
  Adder adder_4 (.a(a[23:16]), .b(b[23:16]), .out(adder_4_out), .cout(adder_4_cout));  // open: cin
  Adder adder_5 (.a(a[23:16]), .b(b[23:16]), .out(adder_5_out), .cin(1'b1), .cout(adder_5_cout));
  Adder adder_6 (.a(a[31:24]), .b(b[31:24]), .out(adder_6_out), .cout(adder_6_cout));  // open: cin
  Adder adder_7 (.a(a[31:24]), .b(b[31:24]), .out(adder_7_out), .cin(1'b1), .cout(adder_7_cout));
  Multiplexer #(.width(8)) multiplexer_1 (.in0(adder_2_out), .in1(adder_3_out), .out(s[15:8]), .sel(adder_1_cout));
  Multiplexer multiplexer_2 (.in0(adder_2_cout), .in1(adder_3_cout), .out(multiplexer_2_out), .sel(adder_1_cout));
  Multiplexer multiplexer_3 (.in0(adder_4_cout), .in1(adder_5_cout), .out(multiplexer_3_out), .sel(multiplexer_2_out));
  Multiplexer #(.width(8)) multiplexer_4 (
    .in0(adder_6_out), .in1(adder_7_out), .out(s[31:24]), .sel(multiplexer_3_out));
  Multiplexer multiplexer_5 (.in0(adder_6_cout), .in1(adder_7_cout), .out(cout), .sel(multiplexer_3_out));
  Multiplexer #(.width(8)) multiplexer_6 (
    .in0(adder_4_out), .in1(adder_5_out), .out(s[23:16]), .sel(multiplexer_2_out));
endmodule

module CsaveA (
  input  cin,
  input  [31:0] a,
  input  [31:0] b,
  input  [31:0] c,
  output [31:0] s,
  output COUT2,
  output COUT1,
  output COUT0
);

  wire CSAAdder_cout;
  wire [31:0] adders_cout, adders_s, shifter_1_out;

  Parallel_FullAdders adders (.a(a), .b(b), .cin(c), .s(adders_s), .cout(adders_cout));
  Shifter #(.width(32)) shifter_1 (.in(adders_cout), .\dist (5'b00001), .out(shifter_1_out));
  CSA CSAAdder (.cin(cin), .a(adders_s), .b(shifter_1_out), .s(s), .cout(CSAAdder_cout));
  and and_1 (COUT2, CSAAdder_cout, adders_cout[31]);
  xor xor_1 (COUT1, CSAAdder_cout, adders_cout[31]);
  nor nor_1 (COUT0, CSAAdder_cout, adders_cout[31]);
endmodule

module Parallel_FullAdders (
  input  [31:0] a,
  input  [31:0] b,
  input  [31:0] cin,
  output [31:0] s,
  output [31:0] cout
);

  wire [31:0] and_1_out, and_2_out, xor_1_out;

  assign and_1_out = a & b;  // AND_Gate and_1, 32 bits wide
  assign xor_1_out = a ^ b;  // XOR_Gate xor_1, 32 bits wide
  assign and_2_out = xor_1_out & cin;  // AND_Gate and_2, 32 bits wide
  assign s = xor_1_out ^ cin;  // XOR_Gate xor_2, 32 bits wide
  assign cout = and_2_out | and_1_out;  // OR_Gate or_1, 32 bits wide
endmodule

module mul (
  input  clk,
  input  start,
  input  [31:0] a,
  input  [31:0] b,
  output done,
  output [63:0] Result
);

  wire and_1_out, comparator_1_gt, comparator_1_lt, CSA_cout1, CSA_cout2, Init, nor_1_out, not_1_out,
       not_2_out, not_3_out, Opperation, or_1_out, or_2_out, or_3_out, or_4_out, or_5_out, OR_R1_FLAG, RE_q,
       RE_signal, signal_1, signal_2, undriven;
  wire [31:0] adder_1_out, CSA2_s, CSA_s, multiplexer_1_out, multiplexer_2_out, multiplexer_3_out,
       multiplexer_4_out, multiplexer_5_out, multiplexer_6_out, R1_q, R2_q, R2_q_2, shifter_1_out,
       shifter_3_out;
  wire [63:0] multiplexer_7_out, multiplexer_8_out, shifter_2_out, shifter_4_out;

  not not_1 (not_1_out, OR_R1_FLAG);
  Multiplexer #(.width(32)) multiplexer_1 (
    .in0({32{1'b0}}), .in1(shifter_2_out[31:0]), .out(multiplexer_1_out), .sel(shifter_1_out[0]));
  Multiplexer #(.width(32)) multiplexer_2 (.in0({32{1'b0}}), .in1(R2_q_2), .out(multiplexer_2_out), .sel(R1_q[0]));
  Multiplexer #(.width(32)) multiplexer_3 (
    .in0({32{1'b0}}), .in1(shifter_2_out[63:32]), .out(multiplexer_3_out), .sel(shifter_1_out[0]));
  nor nor_1 (nor_1_out, Opperation, start);
  and and_1 (and_1_out, not_1_out, Opperation);
  Multiplexer #(.width(32)) multiplexer_4 (.in0({32{1'b0}}), .in1(R2_q), .out(multiplexer_4_out), .sel(R1_q[0]));
  and and_2 (signal_1, Init, start);
  Shifter #(.shift("lr"), .width(32)) shifter_1 (.in(R1_q), .\dist (5'b00001), .out(shifter_1_out));
  or or_1 (or_1_out, nor_1_out, and_1_out);
  and and_3 (signal_2, OR_R1_FLAG, Opperation);
  D_Flip_Flop u_Init (.D(or_1_out), .clk(clk), .Q(Init), .preset(start));  // open: Qn, reset
  D_Flip_Flop u_Opperation (.D(or_2_out), .clk(clk), .Q(Opperation), .reset(undriven));  // open: Qn, preset
  or or_2 (or_2_out, signal_1, signal_2);
  Shifter #(.width(64)) shifter_2 (.in({R2_q_2, R2_q}), .\dist (6'b000001), .out(shifter_2_out));
  CsaveA CSA (
    .a(multiplexer_4_out), .b(multiplexer_1_out), .c(Result[31:0]), .s(CSA_s), .COUT2(CSA_cout2),
    .COUT1(CSA_cout1));  // open: cin, COUT0
  CsaveA CSA2 (
    .cin(or_3_out), .a(multiplexer_2_out), .b(multiplexer_3_out), .c(Result[63:32]), .s(CSA2_s));  // open: COUT2, COUT1, COUT0
  Shifter #(.shift("lr"), .width(32)) shifter_3 (.in(shifter_1_out), .\dist (5'b00001), .out(shifter_3_out));
  Shifter #(.width(64)) shifter_4 (.in(shifter_2_out), .\dist (6'b000001), .out(shifter_4_out));
  or or_3 (or_3_out, CSA_cout2, CSA_cout1);
  Multiplexer #(.width(32)) multiplexer_5 (.in0(CSA2_s), .in1(adder_1_out), .out(multiplexer_5_out), .sel(CSA_cout2));
  Adder #(.width(32)) adder_1 (.a(CSA2_s), .b(32'h1), .out(adder_1_out));  // open: cin, cout
  and and_4 (RE_signal, Opperation, not_2_out);
  not not_2 (not_2_out, OR_R1_FLAG);
  Multiplexer #(.width(32)) multiplexer_6 (.in0(shifter_3_out), .in1(a), .out(multiplexer_6_out), .sel(signal_1));
  or or_4 (or_4_out, signal_1, signal_2);
  Multiplexer #(.width(64)) multiplexer_7 (
    .in0({{32{1'b0}}, b}), .in1(shifter_4_out), .out(multiplexer_7_out), .sel(signal_2));
  or or_5 (or_5_out, RE_signal, signal_1);
  Multiplexer #(.width(64)) multiplexer_8 (
    .in0({64{1'b0}}), .in1({multiplexer_5_out, CSA_s}), .out(multiplexer_8_out), .sel(signal_2));
  Register #(.width(32)) R1 (.D(multiplexer_6_out), .en(or_4_out), .clk(clk), .Q(R1_q));  // open: clr
  Register #(.width(64)) R2 (.D(multiplexer_7_out), .en(or_4_out), .clk(clk), .Q({R2_q_2, R2_q}));  // open: clr
  Register #(.width(64)) R3 (.D(multiplexer_8_out), .en(or_4_out), .clk(clk), .Q(Result));  // open: clr
  Register #(.width(1)) RE (.D(RE_signal), .en(or_5_out), .clk(clk), .Q(RE_q));  // open: clr
  not not_3 (not_3_out, done);
  or or_6 (done, RE_q, RE_signal);
  Comparator #(.width(32)) comparator_1 (
    .a(R1_q), .b({32{1'b0}}), .gt(comparator_1_gt), .lt(comparator_1_lt));  // open: eq
  or or_7 (OR_R1_FLAG, comparator_1_gt, comparator_1_lt);

  // Other names for the same wires on the sheet: IN2[31:0] = b; IN1[31:0] = a; S = start
endmodule

module LSR (
  input  [31:0] a,
  input  [31:0] b,
  output [63:0] shifted
);

  wire comparator_1_eq, not_1_out;
  wire [31:0] multiplexer_1_out, subtractor_1_out;
  wire [63:0] multiplexer_2_out, shifter_1_out, shifter_2_out;

  Subtractor #(.width(32)) subtractor_1 (.a(b), .b(32'h1), .out(subtractor_1_out));  // open: bin, bout
  Multiplexer #(.width(32)) multiplexer_1 (.in0(subtractor_1_out), .in1(b), .out(multiplexer_1_out), .sel(b[0]));
  Comparator #(.width(5)) comparator_1 (.a(b[4:0]), .b({5{1'b0}}), .eq(comparator_1_eq));  // open: gt, lt
  Shifter #(.shift("lr"), .width(64)) shifter_1 (
    .in({{32{1'b0}}, a}), .\dist ({1'b0, multiplexer_1_out[4:0]}), .out(shifter_1_out));
  not not_1 (not_1_out, b[0]);
  Shifter #(.shift("lr"), .width(64)) shifter_2 (.in(shifter_1_out), .\dist (6'b000001), .out(shifter_2_out));
  Multiplexer #(.width(64)) multiplexer_2 (
    .in0(shifter_1_out), .in1(shifter_2_out), .out(multiplexer_2_out), .sel(not_1_out));
  Multiplexer #(.width(64)) multiplexer_3 (
    .in0(multiplexer_2_out), .in1({{32{1'b0}}, a}), .out(shifted), .sel(comparator_1_eq));
endmodule

module LSL (
  input  [31:0] a,
  input  [31:0] b,
  output [63:0] shifted
);

  wire comparator_1_eq, not_1_out;
  wire [31:0] multiplexer_1_out, subtractor_1_out;
  wire [63:0] multiplexer_2_out, shifter_1_out, shifter_2_out;

  Subtractor #(.width(32)) subtractor_1 (.a(b), .b(32'h1), .out(subtractor_1_out));  // open: bin, bout
  Multiplexer #(.width(32)) multiplexer_1 (.in0(subtractor_1_out), .in1(b), .out(multiplexer_1_out), .sel(b[0]));
  Comparator #(.width(5)) comparator_1 (.a(b[4:0]), .b({5{1'b0}}), .eq(comparator_1_eq));  // open: gt, lt
  Shifter #(.width(64)) shifter_1 (.in({{32{1'b0}}, a}), .\dist ({1'b0, multiplexer_1_out[4:0]}), .out(shifter_1_out));
  not not_1 (not_1_out, b[0]);
  Shifter #(.width(64)) shifter_2 (.in(shifter_1_out), .\dist (6'b000001), .out(shifter_2_out));
  Multiplexer #(.width(64)) multiplexer_2 (
    .in0(shifter_1_out), .in1(shifter_2_out), .out(multiplexer_2_out), .sel(not_1_out));
  Multiplexer #(.width(64)) multiplexer_3 (
    .in0(multiplexer_2_out), .in1({{32{1'b0}}, a}), .out(shifted), .sel(comparator_1_eq));
endmodule

module ASR (
  input  [31:0] a,
  input  [31:0] b,
  output [63:0] shifted
);

  wire comparator_1_lt;
  wire [31:0] multiplexer_1_out, not_1_out;
  wire [63:0] LogicalSR_shifted, not_2_out;

  assign not_1_out = ~a;  // NOT_Gate not_1, 32 bits wide
  Comparator #(.width(32)) comparator_1 (.a(a), .b({32{1'b0}}), .lt(comparator_1_lt));  // open: gt, eq
  Multiplexer #(.width(32)) multiplexer_1 (.in0(a), .in1(not_1_out), .out(multiplexer_1_out), .sel(comparator_1_lt));
  LSR LogicalSR (.a(multiplexer_1_out), .b(b), .shifted(LogicalSR_shifted));
  Multiplexer #(.width(64)) multiplexer_2 (
    .in0(LogicalSR_shifted), .in1(not_2_out), .out(shifted), .sel(comparator_1_lt));
  assign not_2_out = ~LogicalSR_shifted;  // NOT_Gate not_2, 64 bits wide
endmodule

module ROT_R (
  input  [31:0] a,
  input  [31:0] b,
  output [63:0] rotated
);

  wire [31:0] subtractor_1_out;
  wire [63:0] Logical_Shift_Left_shifted, Logical_Shift_Right_shifted, or_1_out;

  Subtractor #(.width(32)) subtractor_1 (.a(32'h20), .b(b), .out(subtractor_1_out));  // open: bin, bout
  LSR Logical_Shift_Right (.a(a), .b(b), .shifted(Logical_Shift_Right_shifted));
  LSL Logical_Shift_Left (.a(a), .b(subtractor_1_out), .shifted(Logical_Shift_Left_shifted));
  assign or_1_out = Logical_Shift_Right_shifted | Logical_Shift_Left_shifted;  // OR_Gate or_1, 64 bits wide
  assign rotated = or_1_out & 64'hffffffff;  // AND_Gate and_1, 64 bits wide
endmodule
